# Fritzing sketch Leds- (saved by Fritzing 0.9.3b)
breadboards: 1

parts:
  Componente1 = Arduino Nano (Rev3.0)
  Componente2 = Breakout Board for Electret Microphone
  S1 = Momentary Switch [package=ksa_sealed_tac_switch]
  R1 = Resistor [tolerance=±5% resistance=220 package="0805 [SMD]"]
  U1 = WS2812 RGB LED strip

nets:
  GND: Componente1.GND, Componente2.GND, S1.3, U1.GND
  N1: Componente1.D2, S1.1, R1.Pin_1
  N2: Componente1.D9, U1.DOUT
  VCC: Componente1.5V, Componente2.VCC, R1.Pin_0, U1.VCC
  N3: Componente1.A4, Componente2.AUD

custom parts:
  WS2812 RGB LED strip: WS2812 strip
